# Fritzing sketch coil board (saved by Fritzing 0.9.10b)

parts:
  L1 = Inductors [package=cr54-kit]
  D1 = Rectifier Diode [part_number=1N4001 package="Melf DO-213 AB [SMD]"]
  D3 = Rectifier Diode [part_number=1N4001 package="Melf DO-213 AB [SMD]"]
  D4 = Rectifier Diode [part_number=1N4001 package="Melf DO-213 AB [SMD]"]
  D2 = Rectifier Diode [part_number=1N4001 package="Melf DO-213 AB [SMD]"]
  C1 = Electrolytic Capacitor [capacitance=1µF voltage=35V package="100 mil [THT, electrolytic]"]
  R1 = TRIMPOT [maximum_resistance=10kΩ knob_status=50% power=0.5W package=trimpot_pth_s3_lock]
  J1 = female pin header, 2 pins [form="♀ (female)"]

nets:
  N1: L1.1, D3.cathode, D4.anode
  N2: L1.2, D1.cathode, D2.anode
  N3: D1.anode, D3.anode, C1.-, R1.CCW, J1.pin2
  N4: D4.cathode, D2.cathode, C1.+, R1.CW
  N5: R1.WIPER, J1.pin1
