# Fritzing sketch power distribution board (saved by Fritzing 0.9.10b)

parts:
  M1 = RioRand LM2596
  M2 = RioRand LM2596
  J1 = Screw terminal - 2 pins [package=THT]
  J2 = Screw terminal - 2 pins [package=THT]
  J3 = female pin header, 2 pins [form="♀ (female)"]
  D1 = Diode [package=diode-hv]
  J4 = Screw terminal - 2 pins [package=THT]

nets:
  N1: M1.Pin_1, M2.Pin_2, J1.pin2, J4.pin1
  N2: M1.Pin_2, M2.Pin_1, J1.pin1, J4.pin2
  N3: M1.Pin_3, D1.A
  N4: M1.Pin_4, J3.pin1
  N5: M2.Pin_3, J2.pin1
  N6: M2.Pin_4, J2.pin2
  N7: J3.pin2, D1.C

notes:
  to stepper motor driver
  12-20v input
  to DC motor driver
  to Pi Pico power input
  9v
  3.3v
